# Fritzing sketch barograaf  op protrinket 3v zonder breadboard (saved by Fritzing 0.9.3b)

parts:
  Onderdeel1 = Adafruit_BMP280
  Onderdeel2 = Adafruit Pro Trinket 3.3V 12MHz [part_number="Adafruit #2010"]
  Onderdeel5 = Adafruit DS3231 [part_number="Adafruit #3013"]
  Onderdeel6 = TFT 2.8 inch 320x240 Touch w microSD [part_number=1770]
  U1 = SPDT Slide Switch [package=ayz0202]
  S2 = Momentary Switch [package=ksa_sealed_tac_switch]
  S3 = Momentary Switch [package=ksa_sealed_tac_switch]
  S4 = Momentary Switch [package=ksa_sealed_tac_switch]

nets:
  VIN: Onderdeel1.VIN, Onderdeel5.Vin, Onderdeel6.3.3V
  GND: Onderdeel1.GND, Onderdeel2.GND, Onderdeel5.GND, Onderdeel6.GND, U1.2, S2.1
  N1: Onderdeel1.SCK/SCL, Onderdeel2.A5, Onderdeel5.SCL
  N2: Onderdeel1.SDI/SDA, Onderdeel2.A4, Onderdeel5.SDA
  N3: Onderdeel2.VBUS, Onderdeel6.+5V
  N4: Onderdeel2.D6, S2.3
  N5: Onderdeel2.D5, S4.3
  N6: Onderdeel2.D4, S3.3
  N7: Onderdeel2.D9, Onderdeel6.LCD_DC
  N8: Onderdeel2.D10, Onderdeel6.LCD_CS
  N9: Onderdeel2.D11, Onderdeel6.MOSI
  N10: Onderdeel2.D12, Onderdeel6.MISO
  N11: Onderdeel2.D13, Onderdeel6.SCLK
  N12: Onderdeel6.LCD_LITE, U1.3
  N13: S2.2, S3.2, S4.2

custom parts:
  Adafruit_BMP280: Bosch has stepped up their game with their new BMP280 sensor, an environmental sensor with temperature, barometric pressure that is the next generation upgrade to the BMP085/BMP180/BMP183. This sensor is great for all sorts of weather sensing and can even be used in both I2C and SPI! This precision sensor from Bosch is the best low-cost, precision sensing solution for measuring barometric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
  Adafruit Pro Trinket 3.3V 12MHz: rinket's got a big sister in town - the Pro Trinket 3V! Pro Trinket combines everything you love about Trinket with the familiarity of the core Arduino chip, the ATmega328. It's like an Arduino Pro Mini with more pins and USB tossed in. Trinket's a year old now, and while its been great to see tons of tiny projects, sometimes you just need more pins, more FLASH, and more RAM. That's why we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
  Adafruit DS3231: The datasheet for the DS3231 explains that this part is an "Extremely Accurate I²C-Integrated RTC/TCXO/Crystal". And, hey, it does exactly what it says on the tin! This Real Time Clock (RTC) is the most precise you can get in a small, low power package. Most RTCs use an external 32kHz timing crystal that is used to keep time with low current draw. And that's all well and good, but those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
  TFT 2.8 inch 320x240 Touch w microSD: This TFT display is big (2.8" diagonal) bright (4 white-LED backlight) and colorful! 240x320 pixels with individual RGB pixel control. As a bonus, this display has a resistive touchscreen attached to it already, so you can detect finger presses anywhere on the screen.
